// Logisim project ROM.circ as structural Verilog: 8 circuits, main circuit main
module main (
);

  wire CLOCK, ROM_COEF_ENABLE, ROM_ENABLE;
  wire [15:0] DATA, FILTER_OUT, MUX_OUT, OUT, register_2_q, register_3_q, register_4_q, register_5_q,
       undriven_2;
  wire [15:2] undriven;
  wire [31:0] multiplicador_1_p1, multiplicador_1_p2, multiplicador_1_p3, multiplicador_1_p4,
       multiplicador_1_p5, multiplicador_1_p6, multiplicador_1_p10, multiplicador_1_p13, multiplicador_1_p14,
       multiplicador_1_p15, multiplicador_1_p16, multiplicador_1_p17, multiplicador_1_p18;

  Clock clock_1 (.out(CLOCK));
  SM SM (.Clock(CLOCK), .in_1({undriven, ROM_COEF_ENABLE, ROM_ENABLE}));
  ROM_IN ROM_IN (.Enable(ROM_ENABLE), .Clock(CLOCK), .\Saída (DATA));
  Register #(.width(16)) register_1 (.D(OUT), .en(undriven[10]), .Q(FILTER_OUT), .clk(CLOCK));  // open: clr
  ROM_COE rom_coe_1 (.Enable(ROM_COEF_ENABLE), .Clock(CLOCK), .\Saída (undriven_2));
  REG_COEFS reg_coefs_1 (
    ._0(undriven_2), ._1_2(undriven[2]), ._2_2(undriven[3]), ._3_2(undriven[4]), ._4_2(undriven[5]),
    ._5_2(undriven[6]), ._6_2(undriven[7]), ._1(multiplicador_1_p1), ._2(multiplicador_1_p2),
    ._3(multiplicador_1_p3), ._4(multiplicador_1_p4), ._5(multiplicador_1_p5), ._6(multiplicador_1_p6));
  Multiplexer #(.width(16), .enable("false")) multiplexer_1 (
    .in0(DATA), .in1(FILTER_OUT), .out(MUX_OUT), .sel(undriven[9]));
  ROM_OUT rom_out_1 (.Clock(CLOCK));  // open: Entrada, Enable
  Register #(.width(16)) register_2 (.D(MUX_OUT), .en(undriven[8]), .Q(register_2_q), .clk(CLOCK));  // open: clr
  Register #(.width(16)) register_3 (.D(OUT), .en(undriven[8]), .Q(register_3_q), .clk(CLOCK));  // open: clr
  Register #(.width(16)) register_4 (.D(register_2_q), .en(undriven[8]), .Q(register_4_q), .clk(CLOCK));  // open: clr
  Register #(.width(16)) register_5 (.D(register_3_q), .en(undriven[8]), .Q(register_5_q), .clk(CLOCK));  // open: clr
  // MULTIPLICADOR multiplicador_1: pin names not known; wires that end beside it: multiplicador_1_p1, multiplicador_1_p2, multiplicador_1_p3, multiplicador_1_p4, multiplicador_1_p5, multiplicador_1_p6, MUX_OUT, register_2_q, register_4_q, multiplicador_1_p10, register_3_q, register_5_q, multiplicador_1_p13, multiplicador_1_p14, multiplicador_1_p15, multiplicador_1_p16, multiplicador_1_p17, multiplicador_1_p18
  ADD add_1 (
    .b2(multiplicador_1_p13), .a2(multiplicador_1_p14), .b1(multiplicador_1_p15), .a1(multiplicador_1_p16),
    .b0(multiplicador_1_p17), .a0(multiplicador_1_p18), .\Saída (multiplicador_1_p10));
  Bit_Extender #(.in_width(32), .\type ("sign")) bit_extender_1 (.in(multiplicador_1_p15), .out(OUT));
endmodule

module ROM_IN (
  input  [15:0] \Saída ,
  input  Enable,
  input  Clock
);

  wire [15:0] counter_1_q;

  Counter #(.width(16), .max('h6), .ongoal("stay")) counter_1 (
    .load(1'b0), .count(Enable), .Q(counter_1_q), .clk(Clock));  // open: D, carry, clr
  RAM #(.addrWidth(16), .dataWidth(16)) ram_1 (
    .addr(counter_1_q), .data(\Saída ), .sel(Enable), .clk(Clock), .ld(Enable), .clr(1'b0));
endmodule

module SM (
  input  [15:0] in_1,
  input  Clock
);

  wire [15:0] counter_1_q;

  Counter #(.width(16), .max('h6)) counter_1 (
    .load(1'b0), .count(1'b1), .Q(counter_1_q), .clk(Clock));  // open: D, carry, clr
  RAM #(.addrWidth(16), .dataWidth(16)) ram_1 (
    .addr(counter_1_q), .data(in_1), .sel(1'b1), .clk(Clock), .ld(1'b1), .clr(1'b0));
endmodule

module ROM_OUT (
  input  [15:0] Entrada,
  input  Enable,
  input  Clock
);

  wire [15:0] counter_1_q;

  Counter #(.width(16), .max('h300)) counter_1 (
    .load(1'b0), .count(Enable), .Q(counter_1_q), .clk(Clock));  // open: D, carry, clr
  RAM #(.addrWidth(16), .dataWidth(16)) ram_1 (
    .addr(counter_1_q), .data(Entrada), .sel(Enable), .clk(Clock), .ld(1'b0), .clr(1'b0));
endmodule

module ROM_COE (
  input  [15:0] \Saída ,
  input  Enable,
  input  Clock
);

  wire [15:0] counter_1_q;

  Counter #(.width(16), .max('hc), .ongoal("stay")) counter_1 (
    .load(1'b0), .count(Enable), .Q(counter_1_q), .clk(Clock));  // open: D, carry, clr
  RAM #(.addrWidth(16), .dataWidth(16)) ram_1 (
    .addr(counter_1_q), .data(\Saída ), .sel(Enable), .clk(Clock), .ld(Enable), .clr(1'b0));
endmodule

module REG_COEFS (
  input  [15:0] _0,
  input  [31:0] _1,
  input  _1_2,
  input  [31:0] _2,
  input  _2_2,
  input  [31:0] _3,
  input  _3_2,
  input  [31:0] _4,
  input  _4_2,
  input  [31:0] _5,
  input  _5_2,
  input  [31:0] _6,
  input  _6_2
);

  wire [15:0] register_1_q, register_2_q, register_3_q, register_4_q, register_5_q, register_6_q;

  Register #(.width(16)) register_1 (.D(_0), .en(_1_2), .Q(register_1_q));  // open: clk, clr
  Register #(.width(16)) register_2 (.D(_0), .en(_2_2), .Q(register_2_q));  // open: clk, clr
  Register #(.width(16)) register_3 (.D(_0), .en(_3_2), .Q(register_3_q));  // open: clk, clr
  Register #(.width(16)) register_4 (.D(_0), .en(_4_2), .Q(register_4_q));  // open: clk, clr
  Register #(.width(16)) register_5 (.D(_0), .en(_5_2), .Q(register_5_q));  // open: clk, clr
  Register #(.width(16)) register_6 (.D(_0), .en(_6_2), .Q(register_6_q));  // open: clk, clr
  assign _1 = {{16{register_1_q[15]}}, register_1_q};  // Bit_Extender bit_extender_1
  assign _2 = {{16{register_2_q[15]}}, register_2_q};  // Bit_Extender bit_extender_2
  assign _3 = {{16{register_3_q[15]}}, register_3_q};  // Bit_Extender bit_extender_3
  assign _4 = {{16{register_4_q[15]}}, register_4_q};  // Bit_Extender bit_extender_4
  assign _5 = {{16{register_5_q[15]}}, register_5_q};  // Bit_Extender bit_extender_5
  assign _6 = {{16{register_6_q[15]}}, register_6_q};  // Bit_Extender bit_extender_6
endmodule

// MULTI
module MULTIPLICADOR (
  input  [31:0] _1,
  input  [31:0] _2,
  input  [31:0] _3,
  input  [31:0] _4,
  input  [31:0] _5,
  input  [31:0] _6,
  input  [31:0] M1,
  input  [31:0] _1_2,
  input  [31:0] M2,
  input  [31:0] _2_2,
  input  [31:0] M3,
  input  [31:0] _3_2,
  input  [31:0] M4,
  input  [31:0] _4_2,
  input  [31:0] M5,
  input  [31:0] _5_2,
  input  [31:0] M6,
  input  [31:0] _6_2
);

  Multiplier #(.width(32)) multiplier_1 (.a(M1), .b(_1), .out(_1_2));  // open: cin, cout
  Multiplier #(.width(32)) multiplier_2 (.a(M2), .b(_2), .out(_2_2));  // open: cin, cout
  Multiplier #(.width(32)) multiplier_3 (.a(M3), .b(_3), .out(_3_2));  // open: cin, cout
  Multiplier #(.width(32)) multiplier_4 (.a(M4), .b(_4), .out(_4_2));  // open: cin, cout
  Multiplier #(.width(32)) multiplier_5 (.a(M5), .b(_5), .out(_5_2));  // open: cin, cout
  Multiplier #(.width(32)) multiplier_6 (.a(M6), .b(_6), .out(_6_2));  // open: cin, cout
endmodule

module ADD (
  input  [31:0] b2,
  input  [31:0] \Saída ,
  input  [31:0] a2,
  input  [31:0] b1,
  input  [31:0] a1,
  input  [31:0] b0,
  input  [31:0] a0
);

  wire [31:0] adder_1_out, adder_2_out, adder_3_out, adder_4_out;

  Adder #(.width(32)) adder_1 (.a(b2), .b(a2), .out(adder_1_out));  // open: cin, cout
  Adder #(.width(32)) adder_2 (.a(adder_1_out), .b(b1), .out(adder_2_out));  // open: cin, cout
  Adder #(.width(32)) adder_3 (.a(adder_2_out), .b(a1), .out(adder_3_out));  // open: cin, cout
  Adder #(.width(32)) adder_4 (.a(adder_3_out), .b(b0), .out(adder_4_out));  // open: cin, cout
  Adder #(.width(32)) adder_5 (.a(adder_4_out), .b(a0), .out(\Saída ));  // open: cin, cout
endmodule
